# Fritzing sketch schematic (saved by Fritzing 0.9.4)
circuit board: 10.0251cm x 6.76937cm
breadboards: 1

parts:
  Node_MCU_-_ESP32S = ESP32-38PinWide [part_number=ESP32-38PinWide]
  LDR = Photocell (LDR) [package=THT]
  BMP180 = Barometric Pressure Sensor - BMP180 Breakout (GY-68)
  DHT11 = Humidity and Temperature Sensor DHT11
  R_LDR = Resistor [tolerance=±5% resistance=10k package="0805 [SMD]"]
  R = Resistor [tolerance=±5% resistance=10k package="0805 [SMD]"]

nets:
  VCC: Node_MCU_-_ESP32S.3.3, LDR.pin_1, BMP180.VCC, DHT11.Vcc, R.Pin_1
  GND: Node_MCU_-_ESP32S.GND, BMP180.GND, DHT11.GND, R_LDR.Pin_0
  N1: Node_MCU_-_ESP32S.GPIO6, LDR.pin_0, R_LDR.Pin_1
  N2: Node_MCU_-_ESP32S.GPIO7, Node_MCU_-_ESP32S.GPIO8, BMP180.SCL, BMP180.SDA
  N3: Node_MCU_-_ESP32S.GPIO5, DHT11.Data, R.Pin_0

custom parts:
  ESP32-38PinWide: Generic 38-Pin ESP32 with wide format (only access to one side of pins on a breadboard) based on Stephen Lilley's HiLetgo ESP-WROOM-32 ESP32 ESP-32S Development Board.
  Humidity and Temperature Sensor DHT11: Digital relative humidity & temperature sensor DHT11
