# Fritzing sketch schematic_new (saved by Fritzing 0.9.4)
circuit board: 6.55384cm x 8.00411cm
breadboards: 1

parts:
  BMP180 = Barometric Pressure Sensor - BMP180 Breakout (GY-68)
  LDR = Photocell (LDR) [package=THT]
  R_LDR = Resistor [tolerance=±5% resistance=220 package="1206 [SMD]"]
  R = Resistor [tolerance=±5% resistance=10k package="1206 [SMD]"]
  DHT11 = Humidity and Temperature Sensor DHT11
  NodeMCU_ESP32S = LuaNode32 / ESP32
  10μC_Capacitor = Capacitor [package=cap-pth-small-kit]

nets:
  VCC: BMP180.VCC, LDR.pin_1, R.Pin_0, DHT11.Vcc, NodeMCU_ESP32S.3V3
  GND: BMP180.GND, R_LDR.Pin_1, DHT11.GND, NodeMCU_ESP32S.GND, 10μC_Capacitor.1
  N1: BMP180.SCL, NodeMCU_ESP32S.D22
  N2: BMP180.SDA, NodeMCU_ESP32S.D21
  N3: LDR.pin_0, R_LDR.Pin_0, NodeMCU_ESP32S.D4
  N4: R.Pin_1, DHT11.Data, NodeMCU_ESP32S.D2
  N5: NodeMCU_ESP32S.EN, 10μC_Capacitor.2

custom parts:
  Humidity and Temperature Sensor DHT11: Digital relative humidity & temperature sensor DHT11
  LuaNode32 / ESP32: ESP32 based LuaNode32
